// Logisim project 2_Boolean_Arithmetic.circ as structural Verilog: 2 circuits, main circuit main
module main (
  input  a,
  input  b,
  input  a_2,
  input  b_2,
  input  cin,
  input  a_3,
  input  in_7,
  input  in_8,
  input  in_9,
  input  in_10,
  input  in_11,
  input  in_12,
  input  in_13,
  input  in_14,
  input  in_15,
  input  in_16,
  input  in_17,
  input  in_18,
  input  in_19,
  input  in_20,
  input  in_21,
  input  b_3,
  input  in_23,
  input  in_24,
  input  in_25,
  input  in_26,
  input  in_27,
  input  in_28,
  input  in_29,
  input  in_30,
  input  in_31,
  input  in_32,
  input  in_33,
  input  in_34,
  input  in_35,
  input  in_36,
  input  in_37,
  output sum,
  output carry,
  output sum1,
  output sum_2,
  output cout,
  output Output,
  output out_44,
  output out_45,
  output out_46,
  output out_47,
  output out_48,
  output out_49,
  output out_50,
  output out_51,
  output out_52,
  output out_53,
  output out_54,
  output out_55,
  output out_56,
  output out_57,
  output out_58
);

  wire and_1_out, and_3_out, full_adder_1_cout, full_adder_1_sum, full_adder_2_sum;

  Full_Adder full_adder_1 (
    .a(a_3), .b(b_3), .cin(in_8), .sum(full_adder_1_sum), .cout(full_adder_1_cout));  // open: sum1
  Full_Adder full_adder_2 (.a(in_7), .b(in_8), .cin(in_23), .sum(full_adder_2_sum), .cout(out_45));  // open: sum1
  xor xor_1 (sum1, a_2, b_2);
  and and_1 (and_1_out, a_2, b_2);
  Full_Adder full_adder_3 ();  // open: a, b, cin, sum1, sum, cout
  Full_Adder full_adder_4 ();  // open: a, b, cin, sum1, sum, cout
  Full_Adder full_adder_5 ();  // open: a, b, cin, sum1, sum, cout
  Full_Adder full_adder_6 ();  // open: a, b, cin, sum1, sum, cout
  xor xor_2 (sum, a, b);
  and and_2 (carry, a, b);
  xor xor_3 (sum_2, sum1, cin);
  and and_3 (and_3_out, sum1, cin);
  Full_Adder full_adder_7 ();  // open: a, b, cin, sum1, sum, cout
  Full_Adder full_adder_8 ();  // open: a, b, cin, sum1, sum, cout
  Full_Adder full_adder_9 ();  // open: a, b, cin, sum1, sum, cout
  Full_Adder full_adder_10 ();  // open: a, b, cin, sum1, sum, cout
  Full_Adder full_adder_11 ();  // open: a, b, cin, sum1, sum, cout
  Full_Adder full_adder_12 ();  // open: a, b, cin, sum1, sum, cout
  Full_Adder full_adder_13 ();  // open: a, b, cin, sum1, sum, cout
  Full_Adder full_adder_14 ();  // open: a, b, cin, sum1, sum, cout
  or or_1 (cout, and_1_out, and_3_out);
  Full_Adder full_adder_15 ();  // open: a, b, cin, sum1, sum, cout
  Full_Adder full_adder_16 ();  // open: a, b, cin, sum1, sum, cout
  buf xor_4 (Output, full_adder_1_sum);  // XOR_Gate
  xor xor_5 (out_44, full_adder_2_sum, full_adder_1_cout);

  // Notes on the sheet:
  //   Input
  //   Input
  //   Input
  //   Bitwise XOR
  //   Bitwise AND
  //   Full-Adder
  //   Bitwise XOR
  //   Bitwise AND
  //   Output
  //   Bitwise XOR
  //   Bitwise AND
  //   carry1
  //   carry2
  //   Output
endmodule

module Full_Adder (
  input  a,
  input  b,
  input  cin,
  output sum1,
  output sum,
  output cout
);

  wire and_1_out, and_2_out;

  xor xor_1 (sum1, a, b);
  and and_1 (and_1_out, a, b);
  xor xor_2 (sum, sum1, cin);
  and and_2 (and_2_out, sum1, cin);
  or or_1 (cout, and_1_out, and_2_out);

  // Notes on the sheet:
  //   Input
  //   Bitwise XOR
  //   Bitwise AND
  //   Bitwise XOR
  //   Bitwise AND
  //   carry1
  //   carry2
  //   Output
endmodule
